# Fritzing sketch Bluetooth Client (saved by Fritzing 0.9.3b)
breadboards: 1

parts:
  Part1 = Arduino Uno (Rev3)
  Part2 = Bluetooth Mate Silver
  U1 = LCD-16X2 [package=lcd-16x2]
  LED1 = LED - 5mm [color="Red (633nm)" package="5 mm [THT]"]
  R1 = Resistor [tolerance=±5% resistance=220 package="2010 [SMD]"]
  R2 = Resistor [tolerance=±5% resistance=220 package="2010 [SMD]"]
  J1 = Piezo Speaker
  R4 = Resistor [tolerance=±5% resistance=220 package="2010 [SMD]"]
  R5 = TRIMPOT [package=3386u]

nets:
  N1: Part1.D8, R1.Pin_1
  N2: Part1.D9_PWM, J1.pin2
  N3: Part1.D11_PWM/MOSI, U1.E
  N4: Part1.D12/MISO, U1.RS
  N5: Part1.D2, Part2.VCC
  N6: Part1.D3_PWM, Part2.CTS_5V
  N7: Part1.D4, U1.DB4
  N8: Part1.D5_PWM, U1.DB5
  N9: Part1.D6_PWM, U1.DB6
  N10: Part1.D7, U1.DB7
  5V: Part1.5V, Part2.RX_5V, U1.VDD, R2.Pin_1, R5.CW
  GND: Part1.GND, Part2.TX_5V, U1.VSS, U1.R_W, U1.K, LED1.cathode, R4.Pin_1, R5.CCW
  N11: U1.VO, R5.WIPER
  N12: U1.A, R2.Pin_0
  N13: LED1.anode, R1.Pin_0
  N14: J1.pin1, R4.Pin_0
